# Fritzing sketch electronics (saved by Fritzing 0.9.10b)
circuit board: 8.46667cm x 5.64444cm

parts:
  WeMos_D1_Mini1 = WeMos D1 Mini
  Driver = Camdenboss CTB0158-4 [part_number=CTB0158-4 package=THT]
  Limits = Camdenboss CTB0158-4 [part_number=CTB0158-4 package=THT]
  Encoder = Camdenboss CTB0158-4 [part_number=CTB0158-4 package=THT]
  BTN = Pushbutton [package="[THT]"]
  5V = female pin header, 2 pins [form="♀ (female)"]
  D3 = female pin header, 2 pins [form="♀ (female)"]
  3_3V = female pin header, 2 pins [form="♀ (female)"]
  n2048 = Raspberry Pi 3 [part_number=RPI-3-V1.2]
  NC = female pin header, 2 pins [form="♀ (female)"]  # not connected
  NC_2 = female pin header, 2 pins [form="♀ (female)"]  # not connected

nets:
  N1: WeMos_D1_Mini1.3V3, 3_3V.pin1
  N2: WeMos_D1_Mini1.5V, Limits.pin3, Encoder.pin4, 5V.pin2
  N3: WeMos_D1_Mini1.D0, Limits.pin4
  N4: WeMos_D1_Mini1.D1, Encoder.pin2
  N5: WeMos_D1_Mini1.D2, Encoder.pin1
  N6: WeMos_D1_Mini1.D3, BTN.Pin_3, BTN.Pin_4, D3.pin1
  N7: WeMos_D1_Mini1.D5, Limits.pin2
  N8: WeMos_D1_Mini1.D6, Driver.pin4
  N9: WeMos_D1_Mini1.D7, Driver.pin3
  N10: WeMos_D1_Mini1.D8, Driver.pin2
  GND: WeMos_D1_Mini1.G, Driver.pin1, Limits.pin1, Encoder.pin3, BTN.Pin_1, BTN.Pin_2, D3.pin2, n2048.GND
  N11: WeMos_D1_Mini1.RX, n2048.GIPO14
  N12: WeMos_D1_Mini1.TX, n2048.GIPO15
  5v: 5V.pin1, n2048.5V
  3V3: 3_3V.pin2, n2048.3v3, n2048.3V3

notes:
  D1-B (GREEN)
  D2-A (WHITE)
  GND
  5V
  D5-LSW1
  D0-LSW2
  D8-ENA
  D7-PUL
  D6-DIR
  2023-001
  D3
